# Fritzing sketch agent_board (saved by Fritzing 0.9.3b)
breadboards: 1

parts:
  Raspberry_Pi1 = Raspberry Pi B+
  DS1 = DS18B20 1-Wire Temperature Sensor [part_number=DS18B20]
  R1 = Resistor [tolerance=±5% resistance=4.7 package="0805 [SMD]"]

nets:
  N1: Raspberry_Pi1.3v3, R1.Pin_0
  N2: Raspberry_Pi1.GPIO4, DS1.DQ
  GND: Raspberry_Pi1.GND, DS1.GND
  N3: DS1.VDD, R1.Pin_1
